# Fritzing sketch LabEadUno3_200521 (saved by Fritzing 0.9.3b)
circuit board: 0.27cm x 2cm
circuit board: 5.42748cm x 4.15327cm
circuit board: 5.39469cm x 4.61876cm
circuit board: 0.27cm x 1cm
circuit board: 0.25cm x 2.8cm
circuit board: 2.54398cm x 2.29676cm
circuit board: 0.27cm x 1cm
circuit board: 0.25cm x 2.1cm
circuit board: 0.27cm x 2cm
circuit board: 0.27cm x 1.75cm
circuit board: 8.21772cm x 4.40151cm
circuit board: 0.25cm x 2.2cm
circuit board: 0.27cm x 2cm
breadboards: 1

parts:
  U7 = LM124-324 Quad Opamp [package="DIP (Dual Inline)"]
  R43 = Resistor [tolerance=±5% resistance=10k package=THT]
  R46 = Resistor [tolerance=±5% resistance=10k package=THT]
  R47 = Resistor [tolerance=±5% resistance=10k package=THT]
  R48 = Resistor [tolerance=±5% resistance=10k package=THT]
  C24 = Ceramic Capacitor [capacitance=100nF package="100 mil [THT, multilayer]"]
  C25 = Ceramic Capacitor [capacitance=100nF package="100 mil [THT, multilayer]"]
  Componente1 = Arduino Uno (Rev3) - ICSP  # not connected
  C26 = Ceramic Capacitor [capacitance=100nF package="100 mil [THT, multilayer]"]
  U8 = LM124-324 Quad Opamp [package="DIP (Dual Inline)"]
  C27 = Ceramic Capacitor [capacitance=100nF voltage=50V part_number=47nf package="200 mil [THT, multilayer]"]
  R49 = Resistor [tolerance=±5% resistance=10k package=THT]
  R50 = Resistor [tolerance=±5% resistance=47k package=THT]
  R51 = Resistor [tolerance=±5% resistance=47k package=THT]
  R52 = Resistor [tolerance=±5% resistance=100k package=THT]
  R53 = Resistor [tolerance=±5% resistance=47k package=THT]
  R54 = Resistor [tolerance=±5% resistance=22k package=THT]
  R55 = Resistor [tolerance=±5% resistance=4.7k package=THT]
  R56 = Resistor [tolerance=±5% resistance=100k part_number=180K package=THT]
  R57 = Resistor [tolerance=±5% resistance=330k package=THT]
  R58 = Resistor [tolerance=±5% resistance=10k package=THT]
  R59 = Resistor [tolerance=±5% resistance=100k package=THT]
  R60 = Resistor [tolerance=±5% resistance=100k package=THT]
  R61 = Resistor [tolerance=±5% resistance=10k package=THT]
  Q2 = NPN-Transistor [package="TO92 [THT]"]
  C28 = Tantalum Capacitor [capacitance=10µF package="100 mil [THT, tantalum]"]
  C29 = Tantalum Capacitor [capacitance=47µF package="100 mil [THT, tantalum]"]
  D5 = Diode [package=diode-1n4148]
  D6 = Diode [package=diode-1n4148]
  D7 = Diode [package=diode-1n4148]
  U11 = LM124-324 Quad Opamp [package="DIP (Dual Inline)"]
  C46 = Ceramic Capacitor [capacitance=100nF voltage=50V part_number=47nf package="200 mil [THT, multilayer]"]
  C47 = Ceramic Capacitor [capacitance=100nF voltage=50V part_number=47nf package="200 mil [THT, multilayer]"]
  R78 = Resistor [tolerance=±5% resistance=100k package=THT]
  R79 = Resistor [tolerance=±5% resistance=100k package=THT]
  R80 = Resistor [tolerance=±5% resistance=47k package=THT]
  R81 = Resistor [tolerance=±5% resistance=100k package=THT]
  R82 = Resistor [tolerance=±5% resistance=100k package=THT]
  R83 = Resistor [tolerance=±5% resistance=47k package=THT]
  R84 = Resistor [tolerance=±5% resistance=100k package=THT]
  R85 = Resistor [tolerance=±5% resistance=100k package=THT]
  R86 = Resistor [tolerance=±5% resistance=47k package=THT]
  R87 = Resistor [tolerance=±5% resistance=100k package=THT]
  R88 = Resistor [tolerance=±5% resistance=100k package=THT]
  R89 = Resistor [tolerance=±5% resistance=100k package=THT]
  C48 = Tantalum Capacitor [capacitance=10µF package="100 mil [THT, tantalum]"]
  C23 = Ceramic Capacitor [capacitance=100nF package="100 mil [THT, multilayer]"]
  R90 = Resistor [tolerance=±5% resistance=1k package=THT]
  R91 = Resistor [tolerance=±5% resistance=1k package=THT]
  R92 = Resistor [tolerance=±5% resistance=1k package=THT]
  R93 = Resistor [tolerance=±5% resistance=1k package=THT]
  LED1 = LED - 3mm [color="Red (633nm)" package="3 mm [THT]"]
  LED2 = LED - 3mm [color="Red (633nm)" package="3 mm [THT]"]
  LED3 = LED - 3mm [color="Red (633nm)" package="3 mm [THT]"]
  LED4 = LED - 3mm [color="Red (633nm)" package="3 mm [THT]"]
  R94 = Resistor [tolerance=±5% resistance=10k package=THT]
  Q3 = NPN-Transistor [package="TO92 [THT]"]
  R95 = Resistor [tolerance=±5% resistance=10k package=THT]
  R96 = Resistor [tolerance=±5% resistance=33k part_number=40K package=THT]
  R97 = Resistor [tolerance=±5% resistance=3.3k part_number=3K9 package=THT]

nets:
  N1: U7.1OUT, U7.1IN-
  N2: U7.1IN+, R47.Pin_0, C23.1
  N3: U7.2IN+, R46.Pin_1, C25.0
  N4: U7.2IN-, U7.2OUT
  N5: U7.3OUT, U7.3IN-
  N6: U7.3IN+, R43.Pin_0, C24.1
  GND: U7.VCC-, C24.0, C25.1, C26.1, C23.0
  N7: U7.4IN+, R48.Pin_0, C26.0
  N8: U7.4IN-, U7.4OUT
  Se: U8.1OUT, R52.Pin_1
  N9: U8.1IN-, R51.Pin_0, R52.Pin_0
  N10: U8.1IN+, R50.Pin_1, R53.Pin_0, D6.C, D7.A
  N11: U8.2IN+, R49.Pin_1, C28.+
  N12: U8.2IN-, U8.2OUT, R60.Pin_0, R61.Pin_0
  N13: U8.3OUT, U8.4IN-, C27.1, R53.Pin_1
  N14: U8.3IN-, C27.0, R55.Pin_0, R61.Pin_1
  N15: U8.3IN+, R59.Pin_0, R60.Pin_1
  N16: U8.VCC-, R57.Pin_0, R59.Pin_1, Q2.E, C28.-, C29.-, Q3.E, R96.Pin_0
  N17: U8.4IN+, R56.Pin_0, R57.Pin_1, D5.A
  N18: U8.4OUT, R54.Pin_1, R58.Pin_1, R94.Pin_0
  in: R49.Pin_0, R80.Pin_0, R83.Pin_1
  N19: R50.Pin_0, R51.Pin_1, C29.+, D6.A, D7.C
  N20: R54.Pin_0, D5.C
  N21: R55.Pin_1, Q2.C
  +5V: R56.Pin_1, R95.Pin_0
  N22: R58.Pin_0, Q2.B
  N23: U11.1OUT, R78.Pin_1, R86.Pin_1, R88.Pin_0
  N24: U11.1IN-, R78.Pin_0, R87.Pin_1
  N25: U11.1IN+, C47.1, R80.Pin_1
  N26: U11.2IN+, U11.4IN+, C46.0, C47.0, R79.Pin_1, R83.Pin_0, R87.Pin_0, C48.+
  N27: U11.2IN-, R81.Pin_1, R82.Pin_1, R84.Pin_1
  L2: U11.2OUT, R84.Pin_0
  L3: U11.3OUT, R82.Pin_0, R89.Pin_0
  N28: U11.3IN-, R79.Pin_0, R89.Pin_1
  N29: U11.3IN+, C46.1, R86.Pin_0
  N30: U11.VCC-, C48.-
  N31: U11.4IN-, R85.Pin_0, R88.Pin_1
  L1: U11.4OUT, R81.Pin_0, R85.Pin_1
  N32: R90.Pin_1, LED4.anode
  N33: R91.Pin_1, LED3.anode
  N34: R92.Pin_1, LED2.anode
  N35: R93.Pin_1, LED1.anode
  N36: LED1.cathode, LED2.cathode, LED3.cathode, LED4.cathode
  N37: R94.Pin_1, Q3.B
  N38: Q3.C, R97.Pin_1
  N39: R95.Pin_1, R96.Pin_1, R97.Pin_0

notes:
  LabEadUno3_200521
  LabEAD UNO 3
  UFABC
  5V
  GND
  V0
  V1
  V2
  V3
  V4
  V5
  D4
  D7
  0V
  LabEAD UNO
  3V3
  Vin
  E0
  E1
  E2
  E3
  D/A
  Gerador
  Trifasico
  V6
  V7
  Q
  T
  S
